# Fritzing sketch UXIOPIR (saved by Fritzing 0.9.2b)
breadboards: 1

parts:
  Part1 = Arduino Uno (Rev3)
  U1 = PIR Sensor HC-SR501
  R1 = Resistor [tolerance=±5% resistance=10k package="1206 [SMD]"]

nets:
  N1: Part1.D2, U1.GND, R1.Pin_1
  5V: Part1.5V, U1.VCC, R1.Pin_0
  N2: Part1.GND, U1.OUT

custom parts:
  PIR Sensor HC-SR501: Passive Infra-Red (PIR) sensor HC-SR501
