# Fritzing sketch UXIObutton (saved by Fritzing 0.9.2b)
breadboards: 1

parts:
  Part1 = Arduino Uno (Rev3)
  R1 = Resistor [tolerance=±5% resistance=10k package="1206 [SMD]"]
  S1 = Pushbutton [package="[SMD]"]

nets:
  N1: Part1.D2, R1.Pin_0, S1.Pin_1, S1.Pin_2
  N2: Part1.5V, S1.Pin_3, S1.Pin_4
  N3: Part1.GND, R1.Pin_1
