# Fritzing sketch UXIOpot (saved by Fritzing 0.9.2b)
breadboards: 1

parts:
  Part1 = Arduino Uno (Rev3)
  LED1 = LED - 5mm [color="White (4500K)" package="5 mm [THT]"]
  R1 = Rotary Potentiometer (Small) [maximum_resistance=100kΩ package=THT]

nets:
  N1: Part1.A0, R1.wiper
  N2: Part1.D13/SCK, LED1.anode
  N3: Part1.GND, LED1.cathode, R1.leg2
  N4: Part1.5V, R1.leg1
